# Fritzing sketch StratoSphere2 (saved by Fritzing 0.7.7b)
breadboards: 1

parts:
  R1 = Resistor [tolerance=±5% resistance=220 package=THT]
  T1 = DS18B20 Temperature Sensor [part_number=DS18B20 package="TO92 [THT]"]
  T2 = DS18B20 Temperature Sensor [part_number=DS18B20 package="TO92 [THT]"]
  Arduino1 = Arduino
  Part3 = OpenLog
  50_Channel_D2523T_Helical_GPS_Receiver1 = D2523T-6 - 6 pins
  R11 = 10000 Ω Resistor
  R13 = 10000 Ω Resistor
  R14 = 10000 Ω Resistor
  R15 = Temperature Sensor (Thermistor) [thermistor_type=NTC package=THT]
  R16 = Temperature Sensor (Thermistor) [thermistor_type=NTC package=THT]
  R17 = Temperature Sensor (Thermistor) [thermistor_type=NTC package=THT]
  R18 = Temperature Sensor (Thermistor) [thermistor_type=NTC package=THT]
  R19 = 3.0k Ω Resistor
  LED1 = LED - 3mm [color="Red (633nm)" package="3 mm [THT]"]
  R12 = 10000 Ω Resistor
  R20 = 4.7k Ω Resistor
  S1 = Toggle Switch [package=THT]
  AM1 = AM2302 Humidity and Temperature Sensor

nets:
  N1: R1.Pin_0, Arduino1.D3
  N2: R1.Pin_1, T1.DQ, T2.DQ
  +5V: T1.+Vdd, T2.+Vdd, Arduino1.+5V, S1.COM, AM1.VDD
  GND: T1.GND, T2.GND, Arduino1.GND, Part3.GND, 50_Channel_D2523T_Helical_GPS_Receiver1.GND, R15.pin_1, R16.pin_1, R17.pin_1, R18.pin_1, R19.Pin_1, AM1.GND
  3V3: Arduino1.aref, Arduino1.3V3, Part3.VCC, 50_Channel_D2523T_Helical_GPS_Receiver1.VCC_3.3v, R11.Pin_1, R13.Pin_1, R14.Pin_1, R12.Pin_1
  N3: Arduino1.D9, Part3.RXI
  N4: Arduino1.D8, Part3.TXO
  N5: Arduino1.D5, R20.Pin_1
  N6: Arduino1.D2, AM1.DATA
  N7: Arduino1.D1TX, 50_Channel_D2523T_Helical_GPS_Receiver1.RXI
  N8: Arduino1.D0RX, 50_Channel_D2523T_Helical_GPS_Receiver1.TXO
  N9: Arduino1.A0, R14.Pin_0, R15.pin_0
  N10: Arduino1.A1, R13.Pin_0, R16.pin_0
  N11: Arduino1.A2, R17.pin_0, R12.Pin_0
  N12: Arduino1.A3, R11.Pin_0, R18.pin_0
  N13: 50_Channel_D2523T_Helical_GPS_Receiver1.LED_O, LED1.anode
  N14: R19.Pin_0, LED1.cathode
  N15: R20.Pin_0, S1.L1

custom parts:
  DS18B20 Temperature Sensor: A DS18B20 temperature sensor
  D2523T-6 - 6 pins: The D2523T is a compact GPS smart-antenna engine board, which comes equipped with a Sarantel GeoHelix high-gain active antenna and GPS receiver circuits. The module is based around the high performance 50-channel u-blox 5 platform.
  10000 Ω Resistor: A generic resistor (0.25W)
  3.0k Ω Resistor: A generic resistor (0.25W)
  4.7k Ω Resistor: A generic resistor (0.25W)
